# Fritzing sketch BinaryClock (saved by Fritzing 0.9.0b)
breadboards: 1

parts:
  Part1 = Arduino Mega 2560 (Rev3)
  LED1 = smd LED [color="Red (633nm)" package="0805 [SMD]"]
  LED2 = smd LED [color="Red (633nm)" package="0805 [SMD]"]
  LED3 = smd LED [color="Red (633nm)" package="0805 [SMD]"]
  LED4 = smd LED [color="Red (633nm)" package="0805 [SMD]"]
  LED5 = smd LED [color="Red (633nm)" package="0805 [SMD]"]
  LED6 = smd LED [color="Red (633nm)" package="0805 [SMD]"]
  LED7 = smd LED [color="Green (555nm)" package="0805 [SMD]"]
  LED8 = smd LED [color="Green (555nm)" package="0805 [SMD]"]
  LED9 = smd LED [color="Green (555nm)" package="0805 [SMD]"]
  LED10 = smd LED [color="Green (555nm)" package="0805 [SMD]"]
  R1 = Resistor [tolerance=±5% resistance=330 package="0603 [SMD]"]
  R2 = Resistor [tolerance=±5% resistance=330 package="0603 [SMD]"]
  R3 = Resistor [tolerance=±5% resistance=330 package="0603 [SMD]"]
  R4 = Resistor [tolerance=±5% resistance=330 package="0603 [SMD]"]
  R5 = Resistor [tolerance=±5% resistance=330 package="0603 [SMD]"]
  R6 = Resistor [tolerance=±5% resistance=330 package="0603 [SMD]"]
  R7 = Resistor [tolerance=±5% resistance=330 package="0603 [SMD]"]
  R8 = Resistor [tolerance=±5% resistance=330 package="0603 [SMD]"]
  R9 = Resistor [tolerance=±5% resistance=330 package="0603 [SMD]"]
  R10 = Resistor [tolerance=±5% resistance=330 package="0603 [SMD]"]
  S1 = Momentary Switch [package=ksa_sealed_tac_switch]
  S2 = Momentary Switch [package=ksa_sealed_tac_switch]
  R11 = Resistor [tolerance=±5% resistance=10k package="0603 [SMD]"]
  R12 = Resistor [tolerance=±5% resistance=10k package="0603 [SMD]"]

nets:
  N1: Part1.GND, LED1.cathode, LED2.cathode, LED3.cathode, LED4.cathode, LED5.cathode, LED6.cathode, LED7.cathode, LED8.cathode, LED9.cathode, LED10.cathode, R11.Pin_1, R12.Pin_1
  N2: Part1.5V, S1.4, S2.4
  N3: Part1.D2_PWM, S1.1
  N4: Part1.D3_PWM, S2.1
  N5: Part1.D4_PWM, R7.Pin_1
  N6: Part1.D5_PWM, R8.Pin_1
  N7: Part1.D6_PWM, R9.Pin_1
  N8: Part1.D7_PWM, R10.Pin_1
  N9: Part1.D22, R1.Pin_1
  N10: Part1.D24, R2.Pin_1
  N11: Part1.D26, R3.Pin_1
  N12: Part1.D28, R4.Pin_1
  N13: Part1.D30, R5.Pin_1
  N14: Part1.D32, R6.Pin_1
  N15: LED1.anode, R1.Pin_0
  N16: LED2.anode, R2.Pin_0
  N17: LED3.anode, R3.Pin_0
  N18: LED4.anode, R4.Pin_0
  N19: LED5.anode, R5.Pin_0
  N20: LED6.anode, R6.Pin_0
  N21: LED7.anode, R7.Pin_0
  N22: LED8.anode, R8.Pin_0
  N23: LED9.anode, R9.Pin_0
  N24: LED10.anode, R10.Pin_0
  N25: S1.2, R12.Pin_0
  N26: S2.2, R11.Pin_0
